# Fritzing sketch GemmasHat (saved by Fritzing 0.9.2b)

parts:
  neopixel1 = Neopixel Ring 16
  Part2 = Gemma
  NeoPixel_x_12 = Neopixel Ring 12
  neopixel5 = Neopixel 24 Ring
  Reed_switch_(game) = Reed switch [package=THT]
  Reed_switch_(speed_optional) = Reed switch [package=THT]

nets:
  N1: neopixel1.GND, Part2.GND#18, neopixel5.GND#5, Reed_switch_(game).pin_2, Reed_switch_(speed_optional).pin_1
  N2: neopixel1.VCC, Part2.Vout, neopixel5.Vcc#2
  N3: neopixel1.IN, Part2.D0
  N4: neopixel1.OUT, neopixel5.IN
  N5: Part2.D1, Reed_switch_(game).pin_1
  N6: Part2.D2, Reed_switch_(speed_optional).pin_2
  N7: NeoPixel_x_12.GND, neopixel5.GND#1
  N8: NeoPixel_x_12.VCC, neopixel5.Vcc#6
  N9: NeoPixel_x_12.IN, neopixel5.OUT

custom parts:
  Neopixel Ring 16: Neopixel Ring x16
  Gemma: GEMMA is a tiny wearable platform board with a lot of might in a 1" diameter package. Powered by a Attiny85 and programmable with an Arduino IDE over USB, you'll be able to realize any wearable project!
  Neopixel Ring 12: Neopixel Ring x12
